# Fritzing sketch stm32_servo (saved by Fritzing 0.9.10b)
breadboards: 1

parts:
  J1 = Basic Servo
  Part1 = Arduino Nano (Rev3.0) (ICSP)
  P1 = Multimeter straight red probe
  To_Oscilloscope = Multimeter straight black probe
  VCC2 = 4 x AAA Battery Mount

nets (from the schematic view):
  N1: J1.gnd, To_Oscilloscope.Probe_tip, To_Oscilloscope.Probe_meter_end, VCC2.-
  N2: J1.pulse, Part1.D9, P1.Probe_tip
  N3: Part1.3V3, VCC2.+
